// Logisim project Project.circ as structural Verilog: 6 circuits, main circuit main
module main (
  input  [7:0] Input1,
  input  [7:0] Input2,
  input  [2:0] Opcode,
  input  Clear,
  output [7:0] Output
);

  wire and_1_out, Clk_out, didOperation_q, hasLastResult_q, not_1_out;
  wire [2:0] CL_sel0;
  wire [7:0] adder_1_out, AND8_out_3, multiplexer_1_out, multiplexer_2_out, multiplexer_3_out,
       multiplexer_4_out, multiplier_1_out, NOT8_out_2, OR8_out_3, subtractor_1_out, XOR8_out_3;

  CL CL (
    .op2(Opcode[2]), .op1(Opcode[1]), .op0(Opcode[0]), .clear(Clear), .sel2(CL_sel0[2]), .sel1(CL_sel0[1]),
    .sel0(CL_sel0[0]));
  Multiplexer #(.select(3), .width(8), .enable("false")) multiplexer_1 (
    .in0(adder_1_out), .in1(subtractor_1_out), .in2(multiplier_1_out), .in3(AND8_out_3), .in4(OR8_out_3),
    .in5(XOR8_out_3), .in6(NOT8_out_2), .in7({8{1'b0}}), .out(multiplexer_1_out), .sel(CL_sel0));
  Register lastResult (.D(multiplexer_1_out), .Q(Output), .clk(Clk_out));  // open: en, clr
  Clock Clk (.out(Clk_out));
  Multiplexer #(.width(8), .enable("false")) multiplexer_2 (
    .in0(Input2), .in1(Input1), .out(multiplexer_2_out), .sel(hasLastResult_q));
  Multiplexer #(.width(8), .enable("false")) multiplexer_3 (
    .in0(Input2), .in1(Output), .out(multiplexer_3_out), .sel(hasLastResult_q));
  not not_1 (not_1_out, Clear);
  Adder adder_1 (.a(Input1), .b(multiplexer_3_out), .out(adder_1_out));  // open: cin, cout
  Multiplexer #(.width(8), .enable("false")) multiplexer_4 (
    .in0(Input1), .in1(Output), .out(multiplexer_4_out), .sel(hasLastResult_q));
  Register #(.width(1)) didOperation (.D(not_1_out), .Q(didOperation_q), .clk(Clk_out));  // open: en, clr
  Subtractor subtractor_1 (.a(multiplexer_4_out), .b(multiplexer_2_out), .out(subtractor_1_out));  // open: bin, bout
  Multiplier multiplier_1 (.a(Input1), .b(multiplexer_3_out), .out(multiplier_1_out));  // open: cin, cout
  AND8 AND8 (.in2(Input1), .in1(multiplexer_3_out), .out_3(AND8_out_3));
  Register #(.width(1)) hasLastResult (.D(and_1_out), .Q(hasLastResult_q), .clk(Clk_out));  // open: en, clr
  and and_1 (and_1_out, didOperation_q, ~Clear);  // AND_Gate
  OR8 OR8 (.in2(Input1), .in1(multiplexer_3_out), .out_3(OR8_out_3));
  XOR8 XOR8 (.in2(Input1), .in1(multiplexer_3_out), .out_3(XOR8_out_3));
  NOT8 NOT8 (.in2(multiplexer_4_out), .out_2(NOT8_out_2));
endmodule

module AND8 (
  input  [7:0] in2,
  input  [7:0] in1,
  output [7:0] out_3
);

  assign out_3 = in2 & in1;  // AND_Gate and_1, 8 bits wide
endmodule

module OR8 (
  input  [7:0] in2,
  input  [7:0] in1,
  output [7:0] out_3
);

  assign out_3 = in2 | in1;  // OR_Gate or_1, 8 bits wide
endmodule

module XOR8 (
  input  [7:0] in2,
  input  [7:0] in1,
  output [7:0] out_3
);

  assign out_3 = in2 ^ in1;  // XOR_Gate xor_1, 8 bits wide
endmodule

module NOT8 (
  input  [7:0] in2,
  output [7:0] out_2
);

  assign out_2 = ~in2;  // NOT_Gate not_1, 8 bits wide
endmodule

module CL (
  input  op2,
  input  op1,
  input  op0,
  input  clear,
  output sel2,
  output sel1,
  output sel0
);

  wire and_1_out, and_2_out, and_3_out, and_4_out, and_5_out, and_6_out, and_7_out, and_8_out, and_9_out,
       not_1_out, not_2_out, not_3_out, not_4_out, not_5_out, not_6_out, not_7_out, not_8_out, not_9_out,
       not_10_out, not_11_out;

  not not_1 (not_1_out, op2);
  and and_1 (and_1_out, not_1_out, not_2_out, not_3_out);
  not not_2 (not_2_out, op1);
  not not_3 (not_3_out, op0);
  and and_2 (and_2_out, op2, op0);
  and and_3 (and_3_out, op2, op1);
  not not_4 (not_4_out, op1);
  and and_4 (and_4_out, not_4_out, not_5_out);
  not not_5 (not_5_out, op0);
  not not_6 (not_6_out, op2);
  and and_5 (and_5_out, not_6_out, op1, op0);
  and and_6 (and_6_out, op2, not_7_out);
  not not_7 (not_7_out, op0);
  not not_8 (not_8_out, op2);
  and and_7 (and_7_out, not_8_out, not_9_out);
  not not_9 (not_9_out, op0);
  not not_10 (not_10_out, op1);
  and and_8 (and_8_out, not_10_out, not_11_out);
  not not_11 (not_11_out, op0);
  and and_9 (and_9_out, op2, op1, op0);
  or or_1 (sel2, and_1_out, clear, and_2_out, and_3_out);
  or or_2 (sel1, and_4_out, clear, and_5_out, and_6_out);
  or or_3 (sel0, and_7_out, and_8_out, clear, and_9_out);
endmodule
